# Fritzing sketch Arduino_Uno_Scheme (saved by Fritzing 0.9.3b)
breadboards: 1

parts:
  VCC1 = Battery block 9V
  U1 = ESP8266 WiFi Module [part_number=ESP8266]
  R5 = Resistor [tolerance=±5% resistance=10k package="2512 [SMD]"]
  S1 = Square Pushbutton
  LED1_-_Wifi = smd LED [color="Blue (505nm)" package="1206 [SMD]"]
  LED2_-_Busy = smd LED [color="Red (635nm)" package="1206 [SMD]"]
  R6 = Resistor [tolerance=±5% resistance=220 package="2512 [SMD]"]
  R7 = Resistor [tolerance=±5% resistance=100 package="2512 [SMD]"]
  Componente1 = Arduino Uno (Rev3)

nets:
  GND: VCC1.-, U1.GND, S1.leg0, LED1_-_Wifi.cathode, LED2_-_Busy.cathode, Componente1.GND
  N1: VCC1.+, Componente1.VIN
  N2: U1.RXD, Componente1.D7
  VCC: U1.VCC, U1.CH_PD, Componente1.3V3
  N3: U1.TXD, Componente1.D6_PWM
  N4: R5.Pin_0, S1.leg1, Componente1.D8
  N5: R5.Pin_1, Componente1.5V
  N6: LED1_-_Wifi.anode, R7.Pin_0
  N7: LED2_-_Busy.anode, R6.Pin_0
  N8: R6.Pin_1, Componente1.D5_PWM
  N9: R7.Pin_1, Componente1.D4

custom parts:
  ESP8266 WiFi Module: Generic WiFi Module based on the ESP8266 with onboard PCB antenna and UART communications
