# Fritzing sketch ESP8266_Programmer (saved by Fritzing 0.9.3b)
breadboards: 1

parts:
  USB_FTDI232 = FTDI Basic Programmer
  U2 = ESP8266 WiFi Module [part_number=ESP8266]
  VCC1 = Battery

nets:
  N1: USB_FTDI232.RXI, U2.TXD
  N2: USB_FTDI232.TXO, U2.RXD
  N3: USB_FTDI232.POWER, U2.VCC, VCC1.+
  GND: USB_FTDI232.GND, U2.GND, VCC1.-

custom parts:
  ESP8266 WiFi Module: Generic WiFi Module based on the ESP8266 with onboard PCB antenna and UART communications
