# Fritzing sketch Schema_Arduino_Pro_Mini (saved by Fritzing 0.9.3b)
breadboards: 1

parts:
  VCC1 = Battery block 9V
  Arduino = Arduino Pro Mini (5V)
  U1 = ESP8266 WiFi Module [part_number=ESP8266]
  R5 = Resistor [tolerance=±5% resistance=10k package="2512 [SMD]"]
  S1 = Square Pushbutton
  LED1_-_Wifi = smd LED [color="Blue (505nm)" package="1206 [SMD]"]
  LED2_-_Busy = smd LED [color="Red (635nm)" package="1206 [SMD]"]
  R6 = Resistor [tolerance=±5% resistance=220 package="2512 [SMD]"]
  R7 = Resistor [tolerance=±5% resistance=100 package="2512 [SMD]"]
  LM317 = Voltage Regulator [package=to220-adj]
  C1_220uF = Capacitor Polarized [package=panasonic_c]
  R8 = Resistor [tolerance=±5% resistance=380 package="2512 [SMD]"]
  C1_10uF = Capacitor Polarized [package=panasonic_c]
  R9 = Resistor [tolerance=±5% resistance=390 package="2512 [SMD]"]

nets:
  GND: VCC1.-, Arduino.GND, U1.GND, S1.leg0, LED1_-_Wifi.cathode, LED2_-_Busy.cathode, C1_220uF.-, R8.Pin_0, C1_10uF.-
  N1: VCC1.+, Arduino.RAW, LM317.IN, C1_220uF.+
  N2: Arduino.VCC, R5.Pin_1
  N3: Arduino.D8, R5.Pin_0, S1.leg1
  N4: Arduino.D7, U1.RXD
  N5: Arduino.D6, U1.TXD
  N6: Arduino.D5, R6.Pin_1
  N7: Arduino.D4, R7.Pin_1
  N8: U1.VCC, U1.CH_PD, LM317.OUT, C1_10uF.+, R9.Pin_1
  N9: LED1_-_Wifi.anode, R7.Pin_0
  N10: LED2_-_Busy.anode, R6.Pin_0
  N11: LM317.ADJ, R8.Pin_1, R9.Pin_0

custom parts:
  ESP8266 WiFi Module: Generic WiFi Module based on the ESP8266 with onboard PCB antenna and UART communications
